// Logisim project 4 bit Microprocessor.circ as structural Verilog: 15 circuits, main circuit Final Project
module Final_Project (
  output [3:0] view
);

  wire ACCU_WE, ALU_S0, ALU_S1, ASCII_WE, CLK, REG_WADDR, REG_WE, SOURCE_SELECT, SUB;
  wire [3:0] multiplexer_1_out, Register_File_out_5, Register_File_out_9;
  wire [7:0] counter_1_q, rom_2_data;

  Clock clock_1 (.out(CLK));
  Counter counter_1 (.Q(counter_1_q), .clk(CLK));  // open: load, D, count, carry, clr
  ROM #(.addrWidth(4)) rom_1 (
    .addr(rom_2_data[3:0]), .data({SUB, ALU_S1, ALU_S0, ACCU_WE, SOURCE_SELECT, ASCII_WE, REG_WADDR, REG_WE}));  // open: sel
  ROM rom_2 (.addr(counter_1_q), .data(rom_2_data));  // open: sel
  TTY tty_1 (.data({Register_File_out_9[2:0], Register_File_out_5}), .clk(CLK), .we(ASCII_WE));  // open: clr
  Multiplexer #(.width(4), .enable("false")) multiplexer_1 (
    .in0(rom_2_data[7:4]), .in1(view), .out(multiplexer_1_out), .sel(SOURCE_SELECT));
  Register_File Register_File (
    .IN(multiplexer_1_out), .WE(REG_WE), .CLK(CLK), .Waddr(REG_WADDR), .out_5(Register_File_out_5[0]),
    .out_6(Register_File_out_5[1]), .out_7(Register_File_out_5[2]), .out_8(Register_File_out_5[3]),
    .out_9(Register_File_out_9[0]), .out_10(Register_File_out_9[1]), .out_11(Register_File_out_9[2]),
    .out_12(Register_File_out_9[3]));
  ALU ALU (
    .A0(Register_File_out_9[0]), .A1(Register_File_out_9[1]), .A2(Register_File_out_9[2]),
    .A3(Register_File_out_9[3]), .B0(Register_File_out_5[0]), .B1(Register_File_out_5[1]),
    .B2(Register_File_out_5[2]), .B3(Register_File_out_5[3]), .S0(ALU_S0), .S1(ALU_S1), .OUT(view),
    .CLK(CLK), .WE(ACCU_WE), .SUB(SUB));

  // Notes on the sheet:
  //   Counter
  //   INTSTURCTION DECODER
  //   PROM
  //   contents of rom_1 (hex, n*v repeats v):
  //   0 1 3 4 9 b 10 30 50 70 90
  //   contents of rom_2 (hex, n*v repeats v):
  //   42 81 3 62 51 3 62 c1 3 62 c1 3 62 f1 3 42 22 1 3 42 21 3 42 a1 3 22 1 3 32 31 3 0 22 b1 3 0 32 41 3
  //   0 32 d1 3 0 32 41 6 0 4 32 3 0 22 1 3 0 32 31 3 0 22 a1 3 0 32 31 3 0 32 d1 3 0 32 31 6 0 4 32 6 0 4
  //   3 0 0 22 1 3 0 32 41 3 0 22 d1 3 0 32 31 3 0 32 d1 3 0 32 f1 9 0 4 12 6 0 4 42 6 0 4 32 3 0 22 1 3 0
  //   32 41 3 0 22 d1 3 0 32 31 3 0 32 d1 3 0 42 31 a 0 4 32 3
  //   reg0
  //   reg1
endmodule

module ALU (
  input  SUB,
  input  A0,
  input  A1,
  input  A2,
  input  A3,
  input  B0,
  input  B1,
  input  CLK,
  input  B2,
  input  WE,
  input  B3,
  input  S0,
  input  S1,
  output [3:0] OUT
);

  wire add_sub_1_out_0, add_sub_1_out_1, add_sub_1_out_2, add_sub_1_out_3, and_1_out_0, and_1_out_1,
       and_1_out_2, and_1_out_3, n4_bit_4_1_1_out_19, n4_bit_4_1_1_out_20, n4_bit_4_1_1_out_21,
       n4_bit_4_1_1_out_22, or_1_out_0, or_1_out_1, or_1_out_2, or_1_out_3, xor_1_out_0, xor_1_out_1,
       xor_1_out_2, xor_1_out_3;

  ADD_SUB add_sub_1 (
    .SUB_EN(SUB), .A0(A0), .A1(A1), .A2(A2), .A3(A3), .B0(B0), .B1(B1), .B2(B2), .B3(B3),
    .OUT_0(add_sub_1_out_0), .OUT_1(add_sub_1_out_1), .OUT_2(add_sub_1_out_2), .OUT_3(add_sub_1_out_3));
  OR or_1 (
    .A0(A0), .A1(A1), .A2(A2), .A3(A3), .B0(B0), .B1(B1), .B2(B2), .B3(B3), .OUT_0(or_1_out_0),
    .OUT_1(or_1_out_1), .OUT_2(or_1_out_2), .OUT_3(or_1_out_3));
  AND and_1 (
    .A0(A0), .A1(A1), .A2(A2), .A3(A3), .B0(B0), .B1(B1), .B2(B2), .B3(B3), .OUT_0(and_1_out_0),
    .OUT_1(and_1_out_1), .OUT_2(and_1_out_2), .OUT_3(and_1_out_3));
  XOR xor_1 (
    .A0(A0), .A1(A1), .A2(A2), .A3(A3), .B0(B0), .B1(B1), .B2(B2), .B3(B3), .OUT_0(xor_1_out_0),
    .OUT_1(xor_1_out_1), .OUT_2(xor_1_out_2), .OUT_3(xor_1_out_3));
  _4_BIT_4_1 u_4_bit_4_1_1 (
    .A0(add_sub_1_out_0), .A1(add_sub_1_out_1), .A2(add_sub_1_out_2), .A3(add_sub_1_out_3), .B0(or_1_out_0),
    .B1(or_1_out_1), .B2(or_1_out_2), .B3(or_1_out_3), .C0(and_1_out_0), .C1(and_1_out_1), .C2(and_1_out_2),
    .C3(and_1_out_3), .D0(xor_1_out_0), .D1(xor_1_out_1), .D2(xor_1_out_2), .D3(xor_1_out_3), .S0(S0),
    .S1(S1), .out_19(n4_bit_4_1_1_out_19), .out_20(n4_bit_4_1_1_out_20), .out_21(n4_bit_4_1_1_out_21),
    .out_22(n4_bit_4_1_1_out_22));
  Acumulator2_0 acumulator2_0_1 (
    .A0(n4_bit_4_1_1_out_19), .A1(n4_bit_4_1_1_out_20), .A2(n4_bit_4_1_1_out_21), .A3(n4_bit_4_1_1_out_22),
    .WE(WE), .CLK(CLK), ._0(OUT));
endmodule

module AND (
  input  A0,
  input  A1,
  input  A2,
  input  A3,
  input  B0,
  input  B1,
  input  B2,
  input  B3,
  output OUT_0,
  output OUT_1,
  output OUT_2,
  output OUT_3
);

  and and_1 (OUT_0, A0, B0);
  and and_2 (OUT_1, A1, B1);
  and and_3 (OUT_2, A2, B2);
  and and_4 (OUT_3, A3, B3);
endmodule

module OR (
  input  A0,
  input  A1,
  input  A2,
  input  A3,
  input  B0,
  input  B1,
  input  B2,
  input  B3,
  output OUT_0,
  output OUT_1,
  output OUT_2,
  output OUT_3
);

  or or_1 (OUT_0, A0, B0);
  or or_2 (OUT_1, A1, B1);
  or or_3 (OUT_2, A2, B2);
  or or_4 (OUT_3, A3, B3);
endmodule

module ADD_SUB (
  input  SUB_EN,
  input  A0,
  input  A1,
  input  A2,
  input  A3,
  input  B0,
  input  B1,
  input  B2,
  input  B3,
  output OUT_0,
  output OUT_1,
  output OUT_2,
  output OUT_3
);

  wire full_adder_1_co, full_adder_2_co, full_adder_3_co, xor_1_out, xor_2_out, xor_3_out, xor_4_out;

  xor xor_1 (xor_1_out, B0, SUB_EN);
  xor xor_2 (xor_2_out, B1, SUB_EN);
  xor xor_3 (xor_3_out, B2, SUB_EN);
  full_Adder full_adder_1 (.A(A0), .B(xor_1_out), .CI(SUB_EN), .S(OUT_0), .Co(full_adder_1_co));
  xor xor_4 (xor_4_out, B3, SUB_EN);
  full_Adder full_adder_2 (.A(A1), .B(xor_2_out), .CI(full_adder_1_co), .S(OUT_1), .Co(full_adder_2_co));
  full_Adder full_adder_3 (.A(A2), .B(xor_3_out), .CI(full_adder_2_co), .S(OUT_2), .Co(full_adder_3_co));
  full_Adder full_adder_4 (.A(A3), .B(xor_4_out), .CI(full_adder_3_co), .S(OUT_3));  // open: Co
endmodule

module full_Adder (
  input  A,
  input  B,
  input  CI,
  output S,
  output Co
);

  wire and_1_out, and_2_out, and_3_out;

  xor xor_1 (S, A, B, CI);
  and and_1 (and_1_out, B, CI);
  and and_2 (and_2_out, B, A);
  and and_3 (and_3_out, CI, A);
  or or_1 (Co, and_1_out, and_2_out, and_3_out);
endmodule

module XOR (
  input  A0,
  input  A1,
  input  A2,
  input  A3,
  input  B0,
  input  B1,
  input  B2,
  input  B3,
  output OUT_0,
  output OUT_1,
  output OUT_2,
  output OUT_3
);

  xor xor_1 (OUT_0, A0, B0);
  xor xor_2 (OUT_1, A1, B1);
  xor xor_3 (OUT_2, A2, B2);
  xor xor_4 (OUT_3, A3, B3);
endmodule

module _4_BIT_4_1 (
  input  A0,
  input  A1,
  input  A2,
  input  A3,
  input  B0,
  input  B1,
  input  B2,
  input  B3,
  input  C0,
  input  C1,
  input  C2,
  input  C3,
  input  D0,
  input  D1,
  input  D2,
  input  D3,
  input  S0,
  input  S1,
  output out_19,
  output out_20,
  output out_21,
  output out_22
);

  Multiplexer #(.select(2), .enable("false")) multiplexer_1 (
    .in0(A0), .in1(B0), .in2(C0), .in3(D0), .out(out_19), .sel({S1, S0}));
  Multiplexer #(.select(2), .enable("false")) multiplexer_2 (
    .in0(A1), .in1(B1), .in2(C1), .in3(D1), .out(out_20), .sel({S1, S0}));
  Multiplexer #(.select(2), .enable("false")) multiplexer_3 (
    .in0(A2), .in1(B2), .in2(C2), .in3(D2), .out(out_21), .sel({S1, S0}));
  Multiplexer #(.select(2), .enable("false")) multiplexer_4 (
    .in0(A3), .in1(B3), .in2(C3), .in3(D3), .out(out_22), .sel({S1, S0}));
endmodule

module Acumulator (
  input  A0,
  input  A1,
  input  A2,
  input  A3,
  input  I1,
  input  I0,
  input  CLK,
  input  WE,
  output [3:0] _0,
  output [3:0] _1,
  output [3:0] _2,
  output [3:0] _3
);

  wire and_1_out, and_2_out, and_3_out, and_4_out, decoder_1_out0, decoder_1_out1, decoder_1_out2,
       decoder_1_out3;

  Decoder #(.select(2), .enable("false")) decoder_1 (
    .out0(decoder_1_out0), .out1(decoder_1_out1), .out2(decoder_1_out2), .out3(decoder_1_out3), .sel({I1, I0}));
  and and_1 (and_1_out, decoder_1_out0, WE);
  and and_2 (and_2_out, decoder_1_out1, WE);
  and and_3 (and_3_out, WE, decoder_1_out2);
  and and_4 (and_4_out, WE, decoder_1_out3);
  _4_bit_Register ADD_ACU (
    .Din0(A0), .Din1(A1), .Din1_2(A2), .Din3(A3), .Write(and_1_out), .CLK(CLK), .Dout0(_0[0]), .Dout1(_0[1]),
    .Dout2(_0[2]), .Dout3(_0[3]));
  _4_bit_Register OR_ACU (
    .Din0(A0), .Din1(A1), .Din1_2(A2), .Din3(A3), .Write(and_2_out), .CLK(CLK), .Dout0(_1[0]), .Dout1(_1[1]),
    .Dout2(_1[2]), .Dout3(_1[3]));
  _4_bit_Register AND_ACU (
    .Din0(A0), .Din1(A1), .Din1_2(A2), .Din3(A3), .Write(and_3_out), .CLK(CLK), .Dout0(_2[0]), .Dout1(_2[1]),
    .Dout2(_2[2]), .Dout3(_2[3]));
  _4_bit_Register XOR_ACU (
    .Din0(A0), .Din1(A1), .Din1_2(A2), .Din3(A3), .Write(and_4_out), .CLK(CLK), .Dout0(_3[0]), .Dout1(_3[1]),
    .Dout2(_3[2]), .Dout3(_3[3]));
endmodule

module _4_bit_Register (
  input  Din0,
  input  Din1,
  input  Din1_2,
  input  Din3,
  input  Write,
  input  CLK,
  output Dout0,
  output Dout1,
  output Dout2,
  output Dout3
);

  _1_bit_load_Register u_1_bit_load_register_1 (.Data_In(Din0), .CLK(CLK), .Register_write(Write), .Data_Out(Dout0));
  _1_bit_load_Register u_1_bit_load_register_2 (.Data_In(Din1), .CLK(CLK), .Register_write(Write), .Data_Out(Dout1));
  _1_bit_load_Register u_1_bit_load_register_3 (.Data_In(Din1_2), .CLK(CLK), .Register_write(Write), .Data_Out(Dout2));
  _1_bit_load_Register u_1_bit_load_register_4 (.Data_In(Din3), .CLK(CLK), .Register_write(Write), .Data_Out(Dout3));

  // Other names for the same wires on the sheet: W = Write
endmodule

module _1_bit_load_Register (
  input  Data_In,
  input  CLK,
  input  Register_write,
  output Data_Out
);

  wire multiplexer_1_out;

  Multiplexer #(.enable("false")) multiplexer_1 (
    .in0(Data_Out), .in1(Data_In), .out(multiplexer_1_out), .sel(Register_write));
  D_Flip_Flop d_ff_1 (.clk(CLK), .D(multiplexer_1_out), .Q(Data_Out));  // open: Qn, preset, en, reset
endmodule

module Register_File (
  input  [3:0] IN,
  input  WE,
  input  CLK,
  input  Waddr,
  output out_5,
  output out_6,
  output out_7,
  output out_8,
  output out_9,
  output out_10,
  output out_11,
  output out_12
);

  wire and_1_out, and_2_out, decoder_1_out0, decoder_1_out1;

  Decoder #(.enable("false")) decoder_1 (.out0(decoder_1_out0), .out1(decoder_1_out1), .sel(Waddr));
  and and_1 (and_1_out, WE, decoder_1_out0);
  and and_2 (and_2_out, WE, decoder_1_out1);
  _4_bit_Register u_4_bit_register_1 (
    .Din0(IN[0]), .Din1(IN[1]), .Din1_2(IN[2]), .Din3(IN[3]), .Write(and_1_out), .CLK(CLK), .Dout0(out_5),
    .Dout1(out_6), .Dout2(out_7), .Dout3(out_8));
  _4_bit_Register u_4_bit_register_2 (
    .Din0(IN[0]), .Din1(IN[1]), .Din1_2(IN[2]), .Din3(IN[3]), .Write(and_2_out), .CLK(CLK), .Dout0(out_9),
    .Dout1(out_10), .Dout2(out_11), .Dout3(out_12));
endmodule

// INSTRUCTION DECODER
module Instruction_Decoder (
  input  in_1,
  input  in_2,
  input  in_3,
  input  in_4,
  output out_5,
  output out_6,
  output out_7,
  output out_8,
  output out_9,
  output out_10,
  output out_11,
  output out_12
);

  ROM #(.addrWidth(4)) rom_1 (
    .addr({in_4, in_3, in_2, in_1}), .data({out_12, out_11, out_10, out_9, out_8, out_7, out_6, out_5}));  // open: sel

  // Notes on the sheet:
  //   contents of rom_1 (hex, n*v repeats v):
  //   0 1
endmodule

// ACU
module Acumulator2_0 (
  input  A0,
  input  A1,
  input  A2,
  input  A3,
  input  WE,
  input  CLK,
  output [3:0] _0
);

  _4_bit_Register u_4_bit_register_1 (
    .Din0(A0), .Din1(A1), .Din1_2(A2), .Din3(A3), .Write(WE), .CLK(CLK), .Dout0(_0[0]), .Dout1(_0[1]),
    .Dout2(_0[2]), .Dout3(_0[3]));
endmodule

module PROM (
  input  [7:0] INPUT,
  output [3:0] out_2,
  output [3:0] out_3
);

  ROM rom_1 (.addr(INPUT), .data({out_3, out_2}));  // open: sel

  // Notes on the sheet:
  //   NEEDS PROGRAMED
  //   contents of rom_1 (hex, n*v repeats v):
  //   8 7 6 1 0 0 0 2 0 0 0 3 0 0 0 4 0 0 0 5 0 0 0 6 0 0 0 7 0 0 0 8
endmodule
